# Fritzing sketch rpi-photo-sketch (saved by Fritzing 0.7.12b)
breadboards: 1

parts:
  RaspberryPi1 = Raspberry Pi Model B
  R1 = Resistor [tolerance=±5% resistance=10k package=THT]
  S1 = Pushbutton [package="[THT]"]
  LED1 = LED - 5mm [color="Yellow (595nm)" package="5 mm [THT]"]
  R2 = Resistor [tolerance=±5% resistance=10k package=THT]
  S2 = Pushbutton [package="[THT]"]
  R3 = Resistor [tolerance=±5% resistance=68 package=THT]

nets:
  N1: RaspberryPi1.3V3, RaspberryPi1.SDA, R1.Pin_0, R2.Pin_0
  N2: RaspberryPi1.GND, RaspberryPi1.TXD, S1.Pin_1, S1.Pin_2, LED1.cathode, S2.Pin_1, S2.Pin_2
  N3: RaspberryPi1.#17, RaspberryPi1.#21, R1.Pin_1, S1.Pin_3, S1.Pin_4
  N4: RaspberryPi1.#23, RaspberryPi1.#24, R2.Pin_1, S2.Pin_3, S2.Pin_4
  N5: RaspberryPi1.#25, RaspberryPi1.CS0, R3.Pin_0
  N6: LED1.anode, R3.Pin_1

custom parts:
  Raspberry Pi Model B: Raspberry Pi (Model B)
